# Fritzing sketch Schaltplan (saved by Fritzing 0.9.4)

parts:
  Bauteil1 = Arduino Nano (Rev3.0)
  U1 = WS2812 RGB LED strip
  Part1 = SCD30

nets:
  N1: Bauteil1.D6, U1.DIN
  GND: Bauteil1.GND, U1.GND, Part1.GND
  5V: Bauteil1.5V, U1.VCC, Part1.VDD
  N2: Bauteil1.A5, Part1.TX/SCL
  N3: Bauteil1.A4, Part1.RX/SDA

custom parts:
  WS2812 RGB LED strip: WS2812 strip
  SCD30: CO2 , humidity, and temperature sensor * Current consumption: 19 mA @ 1 meas. per 2 s. * Digital interface UART or I2C * Company: Sensirion - The Sensor Company Electrical specifications * average current: 19 mA * max. current: 75 mA * DC supply: 3.3 V - 5.5 V Operation conditions * temperature: 0 – 50°C * humidity: 0 – 95 %RH * sensor lifetime: 15 years CO2-sensor: * NDIR CO 2 sensor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
